// Logisim project s-mips.circ as structural Verilog
module S_MIPS_Board (
  input  DESHABILITAR_DISPATCHER,
  output halt
);

  wire button_1_out, CLK, CS, d_ff_1_q, LCLR, LoadRAM, LoadRAMOn, LW, R_R_W, R_W, ram_dispatcher_1_finished,
       RCS, Reset_out, RST, TTY_EN;
  wire [2:0] KDB;
  wire [3:0] LMask, Mask, ram_1_read_time, ram_1_write_time, RMask;
  wire [6:0] KDB_DATA, TTY_DATA;
  wire [15:0] Addr, LAddr, RAddr;
  wire [31:0] I0, I1, I2, I3, LData, ram_1_data_out_0, ram_1_data_out_1, ram_1_data_out_2, ram_1_data_out_3,
       RI0, RI1, RI2, RI3;

  TTY #(.rows(25), .cols(80)) tty_1 (.data(TTY_DATA), .clk(CLK), .we(TTY_EN), .clr(RST));
  not not_1 (LoadRAMOn, ram_dispatcher_1_finished);
  RAM_Dispatcher ram_dispatcher_1 (
    .WriteTime(ram_1_write_time), .Clock(CLK), .Data(LData), .Address(LAddr), .Mask(LMask),
    .Finished(ram_dispatcher_1_finished), .Write(LW), .CLR(LCLR));
  Keyboard #(.buflen(64)) keyboard_1 (.clk(CLK), .re(KDB[0]), .avail(KDB[2]), .data(KDB_DATA));  // open: clr
  RAM ram_1 (
    .Address(RAddr), .Data_Out_0(ram_1_data_out_0), .Data_Out_1(ram_1_data_out_1),
    .Data_Out_2(ram_1_data_out_2), .Data_Out_3(ram_1_data_out_3), .Data_In_0(RI0), .Data_In_1(RI1),
    .Data_In_2(RI2), .Data_In_3(RI3), .Mask(RMask), .nRead_Write(R_R_W), .Chip_Select(RCS),
    .Read_Time(ram_1_read_time), .Reset(button_1_out), .Write_Time(ram_1_write_time));
  Button button_1 (.out(button_1_out));
  D_Flip_Flop d_ff_1 (.clk(CLK), .D(1'b1), .Q(d_ff_1_q), .reset(Reset_out));  // open: Qn, preset, en
  Button Reset (.out(Reset_out));
  S_MIPS s_mips_1 (
    .Kbd_Enable(KDB[0]), .Address(Addr), .Kbd_Clear(KDB[1]), .Kbd_Available(KDB[2]), .RAM_In_0(I0),
    .Kbd_ASCII_Data(KDB_DATA), .RAM_In_1(I1), .TTY_Enable(TTY_EN), .RAM_In_2(I2), .RAM_In_3(I2),
    .TTY_ASCII_Data(TTY_DATA), .Reset(RST), .RAM_Out_0(ram_1_data_out_0), .Clock(CLK),
    .RAM_Out_1(ram_1_data_out_1), .Stop(halt), .RAM_Out_2(ram_1_data_out_2), .RAM_Out_3(ram_1_data_out_3),
    .Mask(Mask), .Read_Time(ram_1_read_time), .Write_Time(ram_1_write_time), .nRead_Write(R_W),
    .Chip_Select(CS));
  D_Flip_Flop d_ff_2 (.clk(CLK), .D(d_ff_1_q), .Qn(LCLR), .reset(Reset_out));  // open: Q, preset, en
  or or_1 (RST, LCLR, LoadRAM);
  Clock clock_1 (.out(CLK));
  Multiplexer #(.width(32), .enable("false")) multiplexer_1 (.in0(I0), .in1(LData), .out(RI0), .sel(LoadRAM));
  Multiplexer #(.width(32), .enable("false")) multiplexer_2 (.in0(I1), .in1(LData), .out(RI1), .sel(LoadRAM));
  Multiplexer #(.width(32), .enable("false")) multiplexer_3 (.in0(I2), .in1(LData), .out(RI2), .sel(LoadRAM));
  Multiplexer #(.width(32), .enable("false")) multiplexer_4 (.in0(I3), .in1(LData), .out(RI3), .sel(LoadRAM));
  and and_1 (LoadRAM, ~DESHABILITAR_DISPATCHER, LoadRAMOn);  // AND_Gate
  Multiplexer #(.width(16), .enable("false")) multiplexer_5 (.in0(Addr), .in1(LAddr), .out(RAddr), .sel(LoadRAM));
  Multiplexer #(.width(4), .enable("false")) multiplexer_6 (.in0(Mask), .in1(LMask), .out(RMask), .sel(LoadRAM));
  Multiplexer #(.enable("false")) multiplexer_7 (.in0(CS), .in1(LW), .out(RCS), .sel(LoadRAM));
  Multiplexer #(.enable("false")) multiplexer_8 (.in0(R_W), .in1(LW), .out(R_R_W), .sel(LoadRAM));

  // Notes on the sheet:
  //   NO MODIFICAR
  //   Keyboard
endmodule

module RAM (
  input  [15:0] Address,
  input  [31:0] Data_In_0,
  input  [31:0] Data_In_1,
  input  [31:0] Data_In_2,
  input  [31:0] Data_In_3,
  input  [3:0] Mask,
  input  nRead_Write,
  input  Chip_Select,
  input  Reset,
  output [31:0] Data_Out_0,
  output [31:0] Data_Out_1,
  output [31:0] Data_Out_2,
  output [31:0] Data_Out_3,
  output [3:0] Read_Time,
  output [3:0] Write_Time
);

  wire and_2_out, and_3_out, and_4_out, and_5_out, and_6_out, and_7_out, and_8_out, and_9_out, Changed, CLK,
       comparator_2_eq, comparator_3_eq, comparator_4_eq, comparator_5_eq, comparator_6_eq, Count,
       demultiplexer_3_out0, Idle, Idle_q, Load, Load0, Load1, nand_1_out, or_1_out, or_2_out, or_3_out,
       or_4_out, or_5_out, or_6_out, or_7_out, or_8_out, or_9_out, or_10_out, Proc_q, Update_Mem, Zero_Time;
  wire [3:0] counter_1_q, multiplexer_1_out, subtractor_1_out;
  wire [31:0] register_1_q, register_2_q, register_3_q, register_4_q, register_5_q;

  // Probe on 4'b0011
  // Probe on 4'b0010
  Multiplexer #(.width(4), .enable("false")) multiplexer_1 (
    .in0(4'b0011), .in1(4'b0010), .out(multiplexer_1_out), .sel(nRead_Write));
  or or_1 (or_1_out, Idle, Update_Mem);
  or or_2 (or_2_out, ~Chip_Select, Reset);  // OR_Gate
  Subtractor #(.width(4)) subtractor_1 (.a(multiplexer_1_out), .b(4'b0010), .out(subtractor_1_out));  // open: bin, bout
  Demultiplexer #(.enable("false")) demultiplexer_1 (.out0(Idle), .out1(Load0), .in(Idle_q), .sel(Changed));
  D_Flip_Flop u_Idle (.clk(CLK), .D(or_1_out), .Q(Idle_q), .preset(or_2_out));  // open: Qn, en, reset
  // Probe on counter_1_q
  Counter #(.width(4), .max('hf)) counter_1 (
    .load(Load), .D(subtractor_1_out), .count(Count), .Q(counter_1_q), .clk(CLK), .clr(or_3_out));  // open: carry
  or or_3 (or_3_out, ~Chip_Select, Reset);  // OR_Gate
  Comparator #(.width(4), .mode("unsigned")) comparator_1 (
    .a(4'b0000), .b(counter_1_q), .eq(Zero_Time));  // open: gt, lt
  or or_4 (or_4_out, Count, Load0, Load1);
  Register #(.width(32)) register_1 (.D(Data_In_0), .en(Chip_Select), .Q(register_1_q), .clk(CLK), .clr(or_5_out));
  or or_5 (or_5_out, ~Chip_Select, Reset);  // OR_Gate
  Register #(.width(32)) register_2 (.D(Data_In_1), .en(Chip_Select), .Q(register_2_q), .clk(CLK), .clr(or_6_out));
  or or_6 (or_6_out, ~Chip_Select, Reset);  // OR_Gate
  Register #(.width(32)) register_3 (.D(Data_In_2), .en(Chip_Select), .Q(register_3_q), .clk(CLK), .clr(or_7_out));
  or or_7 (or_7_out, ~Chip_Select, Reset);  // OR_Gate
  Register #(.width(32)) register_4 (.D(Data_In_3), .en(Chip_Select), .Q(register_4_q), .clk(CLK), .clr(or_8_out));
  or or_8 (or_8_out, ~Chip_Select, Reset);  // OR_Gate
  Register #(.width(32)) register_5 (
    .D({{11{1'b1}}, nRead_Write, Mask, Address}), .en(Chip_Select), .Q(register_5_q), .clk(CLK),
    .clr(or_9_out));
  or or_9 (or_9_out, ~Chip_Select, Reset);  // OR_Gate
  D_Flip_Flop Proc (.clk(CLK), .D(or_4_out), .Q(Proc_q), .reset(or_10_out));  // open: Qn, preset, en
  or or_10 (or_10_out, ~Chip_Select, Reset);  // OR_Gate
  Demultiplexer #(.enable("false")) demultiplexer_2 (
    .out0(Count), .out1(Update_Mem), .in(demultiplexer_3_out0), .sel(Zero_Time));
  Demultiplexer #(.enable("false")) demultiplexer_3 (
    .out0(demultiplexer_3_out0), .out1(Load1), .in(Proc_q), .sel(Changed));
  Clock clock_1 (.out(CLK));
  Comparator #(.width(32)) comparator_2 (.a(register_1_q), .b(Data_In_0), .eq(comparator_2_eq));  // open: gt, lt
  Comparator #(.width(32)) comparator_3 (.a(register_2_q), .b(Data_In_1), .eq(comparator_3_eq));  // open: gt, lt
  Comparator #(.width(32)) comparator_4 (.a(register_3_q), .b(Data_In_2), .eq(comparator_4_eq));  // open: gt, lt
  Comparator #(.width(32)) comparator_5 (.a(register_4_q), .b(Data_In_3), .eq(comparator_5_eq));  // open: gt, lt
  Comparator #(.width(32)) comparator_6 (
    .a(register_5_q), .b({{11{1'b1}}, nRead_Write, Mask, Address}), .eq(comparator_6_eq));  // open: gt, lt
  nand nand_1 (nand_1_out, comparator_6_eq, comparator_2_eq, comparator_3_eq, comparator_4_eq, comparator_5_eq);
  and and_1 (Changed, nand_1_out, Chip_Select);
  or or_11 (Load, Count, Load1, Load0);
  and and_2 (and_2_out, Mask[0], Update_Mem, nRead_Write);
  and and_3 (and_3_out, Mask[1], Update_Mem, nRead_Write);
  and and_4 (and_4_out, Mask[2], Update_Mem, nRead_Write);
  and and_5 (and_5_out, Mask[3], Update_Mem, nRead_Write);
  RAM_part #(.addrWidth(16), .dataWidth(32), .bus("separate")) ram_1 (
    .addr(Address), .din(Data_In_0), .data(Data_Out_0), .str(and_2_out), .sel(Chip_Select), .clk(CLK),
    .ld(and_6_out), .clr(Reset));
  and and_6 (and_6_out, ~nRead_Write, Idle);  // AND_Gate
  RAM_part #(.addrWidth(16), .dataWidth(32), .bus("separate")) ram_2 (
    .addr(Address), .din(Data_In_1), .data(Data_Out_1), .str(and_3_out), .sel(Chip_Select), .clk(CLK),
    .ld(and_7_out), .clr(Reset));
  and and_7 (and_7_out, ~nRead_Write, Idle);  // AND_Gate
  RAM_part #(.addrWidth(16), .dataWidth(32), .bus("separate")) ram_3 (
    .addr(Address), .din(Data_In_2), .data(Data_Out_2), .str(and_4_out), .sel(Chip_Select), .clk(CLK),
    .ld(and_8_out), .clr(Reset));
  and and_8 (and_8_out, ~nRead_Write, Idle);  // AND_Gate
  RAM_part #(.addrWidth(16), .dataWidth(32), .bus("separate")) ram_4 (
    .addr(Address), .din(Data_In_3), .data(Data_Out_3), .str(and_5_out), .sel(Chip_Select), .clk(CLK),
    .ld(and_9_out), .clr(Reset));
  and and_9 (and_9_out, ~nRead_Write, Idle);  // AND_Gate

  assign Read_Time = 4'b0011;
  assign Write_Time = 4'b0010;

  // Other names for the same wires on the sheet: M0 = Mask[0]; M1 = Mask[1]; M2 = Mask[2]; M3 = Mask[3];
  //   RW = nRead_Write; CLR = Reset; CS = Chip_Select; Load2 = Count

  // Notes on the sheet:
  //   NO MODIFICAR
  //   excepto quizás los valores RT y WT
  //   BANK0
  //   BANK1
  //   BANK2
  //   BANK3
endmodule

module S_MIPS (
  input  Kbd_Available,
  input  [6:0] Kbd_ASCII_Data,
  input  [31:0] RAM_Out_0,
  input  [31:0] RAM_Out_1,
  input  Reset,
  input  [31:0] RAM_Out_2,
  input  Clock,
  input  [31:0] RAM_Out_3,
  input  [3:0] Read_Time,
  input  [3:0] Write_Time,
  output Kbd_Enable,
  output [15:0] Address,
  output Kbd_Clear,
  output TTY_Enable,
  output [6:0] TTY_ASCII_Data,
  output Stop,
  output [31:0] RAM_In_0,
  output [31:0] RAM_In_1,
  output [31:0] RAM_In_2,
  output [31:0] RAM_In_3,
  output [3:0] Mask,
  output nRead_Write,
  output Chip_Select
);

  wire [31:0] Instruction, LDLR;

  instruction_decoder instruction_decoder_1 (.in_1(Instruction));  // open: K, Save_in_registers, jump, Op, W, DA, R, A, B
  GET_RAM_ADRESS get_ram_adress_1 (.in_4(Clock), .RAM_Address(Address));  // open: in_1, in_2, in_3, in_5, in_6
  GetInstruction getinstruction_1 (
    .in_1(RAM_In_0), .in_8(Read_Time), .in_2(RAM_In_1), .in_3(RAM_In_2), .in_5(RAM_In_3), .in_4(Instruction),
    .in_6(LDLR), .in_7(Clock));  // open: in_9, in_10

  // Other names for the same wires on the sheet: CLK = Clock; CLR = Reset; CS = Chip_Select;
  //   KBD_AVAIL = Kbd_Available; KBD_CLR = Kbd_Clear; KBD_DATA[6:0] = Kbd_ASCII_Data; RAM_A[15:0] = Address;
  //   RAM_INPUT_0[31:0] = RAM_In_0; RAM_INPUT_1[31:0] = RAM_In_1; RAM_INPUT_2[31:0] = RAM_In_2;
  //   RAM_INPUT_3[31:0] = RAM_In_3; RAM_MASK[3:0] = Mask; RAM_OUTPUT_0[31:0] = RAM_Out_0;
  //   RAM_OUTPUT_1[31:0] = RAM_Out_1; RAM_OUTPUT_2[31:0] = RAM_Out_2; RAM_OUTPUT_3[31:0] = RAM_Out_3;
  //   RW = nRead_Write; TTY_DATA[6:0] = TTY_ASCII_Data

  // Notes on the sheet:
  //   RAM ADDRESS
  //   DATA FROM RAM
  //   DATA TO RAM
  //   DATA WRITE MASK
  //   RAM TIMING
  //   RAM CONTROL
  //   KEYBOARD
  //   TTY
  //   SEQUENCING
  //   LDLR: Leido de la RAM 
endmodule

module RAM_Dispatcher (
  input  [3:0] WriteTime,
  input  Clock,
  input  CLR,
  output [31:0] Data,
  output [15:0] Address,
  output [3:0] Mask,
  output Finished,
  output Write
);

  wire demultiplexer_2_out1, demultiplexer_3_out1, End, IDLE_q, IncAddr, Load, or_1_out, or_2_out, While_q,
       WriteEnd;
  wire [3:0] counter_1_q;
  wire [31:0] CurrentAddress_q;

  Counter #(.width(32), .max('hffffffff)) CurrentAddress (
    .count(IncAddr), .Q({CurrentAddress_q[31:18], Address, CurrentAddress_q[1:0]}), .clk(Clock), .clr(CLR));  // open: load, D, carry
  or or_1 (or_1_out, IncAddr, demultiplexer_3_out1, Finished);
  D_Flip_Flop IDLE (.clk(Clock), .D(or_1_out), .Q(IDLE_q), .preset(CLR));  // open: Qn, en, reset
  Demultiplexer #(.enable("false")) demultiplexer_1 (.out0(Load), .out1(Finished), .in(IDLE_q), .sel(End));
  D_Flip_Flop While (.clk(Clock), .D(or_2_out), .Q(While_q), .reset(CLR));  // open: Qn, preset, en
  or or_2 (or_2_out, Write, Load);
  RAM_part #(.addrWidth(18), .dataWidth(32)) ram_1 (
    .addr({Address, CurrentAddress_q[1:0]}), .data(Data), .clk(Clock));  // open: sel, ld, clr
  Demultiplexer #(.enable("false")) demultiplexer_2 (
    .out0(Write), .out1(demultiplexer_2_out1), .in(While_q), .sel(WriteEnd));
  Decoder #(.select(2)) decoder_1 (
    .out0(Mask[0]), .out1(Mask[1]), .out2(Mask[2]), .out3(Mask[3]), .sel(CurrentAddress_q[1:0]));  // open: en
  Demultiplexer #(.enable("false")) demultiplexer_3 (
    .out0(IncAddr), .out1(demultiplexer_3_out1), .in(demultiplexer_2_out1), .sel(End));
  Counter #(.width(4), .max('hf)) counter_1 (
    .load(Load), .D(WriteTime), .count(Write), .Q(counter_1_q), .clk(Clock));  // open: carry, clr
  Comparator #(.width(32)) comparator_1 (.a(Data), .b({32{1'b1}}), .eq(End));  // open: gt, lt
  Comparator #(.width(4)) comparator_2 (.a(4'b0000), .b(counter_1_q), .eq(WriteEnd));  // open: gt, lt

  // Other names for the same wires on the sheet: CLK = Clock; Count = Write; WT[3:0] = WriteTime
endmodule

// Saca 1 cuando termino de cargar la instruccion
module GetInstruction (
  input  [31:0] in_1,
  input  [31:0] in_2,
  input  [31:0] in_3,
  input  [31:0] in_4,
  input  [31:0] in_5,
  input  [31:0] in_6,
  input  in_7,
  input  [3:0] in_8,
  input  in_9,
  input  in_10
);

  wire cronometro_1_output, Enable;

  InstructionLoad instructionload_1 (.in_1(in_1), .in_2(in_2), .in_3(in_3), .in_4(in_5), .out_5(in_4));
  Cronometro cronometro_1 (
    .in_1(in_8), .Activo(1'b1), .Output(cronometro_1_output), .Reloj(in_7), .Enable(Enable));  // open: Start, Counting
  Multiplexer #(.width(32), .enable("false")) multiplexer_1 (
    .in0(32'h1000ffff), .in1(in_4), .out(in_6), .sel(cronometro_1_output));
  or or_1 (Enable, in_9, in_10);

  // Other names for the same wires on the sheet: CLK = in_7; RT[3:0] = in_8

  // Notes on the sheet:
  //   B0
  //   B1
  //   B2
  //   B3
  //   1 cuando termina de cargar la instruccion
  //   Ciclo infinito para ignorar ordenes
  //   READED FROM RAM
  //   NEXT INSTRUCTION
endmodule

module InstructionLoad (
  input  [31:0] in_1,
  input  [31:0] in_2,
  input  [31:0] in_3,
  input  [31:0] in_4,
  output [31:0] out_5
);


  assign out_5 = {in_4[7:0], in_3[7:0], in_2[7:0], in_1[7:0]};
endmodule

module Cronometro (
  input  [3:0] in_1,
  input  Start,
  input  Activo,
  input  Enable,
  input  Reloj,
  output Output,
  output Counting
);

  wire comparator_1_gt, comparator_1_lt, comparator_2_lt, or_1_out, or_2_out, or_3_out, t_ff_1_q;
  wire [4:0] counter_1_q;

  or or_1 (or_1_out, Output, Start);
  T_Flip_Flop t_ff_1 (.clk(Reloj), .T(or_1_out), .Q(t_ff_1_q));  // open: Qn, preset, reset, en
  or or_2 (or_2_out, t_ff_1_q, Activo);
  Counter #(.width(5), .max('h1f)) counter_1 (
    .count(or_2_out), .Q(counter_1_q), .clk(Reloj), .clr(or_3_out));  // open: load, D, carry
  Comparator #(.width(5)) comparator_1 (
    .a(counter_1_q), .b({5{1'b0}}), .gt(comparator_1_gt), .lt(comparator_1_lt));  // open: eq
  Comparator #(.width(5)) comparator_2 (
    .a({1'b0, in_1}), .b(counter_1_q), .eq(Output), .lt(comparator_2_lt));  // open: gt
  or or_3 (or_3_out, comparator_2_lt, Enable);
  or or_4 (Counting, comparator_1_gt, comparator_1_lt, Start);

  // Notes on the sheet:
  //   Cronometro: Devuelve 1 cuando pasan
  //   Tantos ciclos de reloj
  //   Como indica la entrada
endmodule

module GET_RAM_ADRESS (
  input  in_1,
  input  in_2,
  input  [31:0] in_3,
  input  in_4,
  input  [15:0] in_5,
  input  [15:0] in_6,
  output [15:0] RAM_Address
);

  wire [15:0] Read_From, Write_in;

  Register #(.width(16)) register_1 (.D(in_5), .en(in_2), .Q(Read_From), .clk(in_4));  // open: clr
  Register #(.width(16)) register_2 (.D(in_6), .en(in_1), .Q(Write_in), .clk(in_4));  // open: clr
  Multiplexer #(.select(2), .width(16)) multiplexer_1 (
    .in0(in_3[15:0]), .in1(Read_From), .in2(Write_in), .out(RAM_Address), .sel({in_1, in_2}));  // open: in3, en

  // Other names for the same wires on the sheet: R = in_2; W = in_1; CLK = in_4; Next[15:0] = in_3[15:0]

  // Notes on the sheet:
  //   PC INSTRUCTION
  //   READ INSTRUCTION
  //   WRITE INSTRUCTION
endmodule

module instruction_decoder (
  input  [31:0] in_1,
  output [15:0] K,
  output Save_in_registers,
  output jump,
  output [4:0] Op,
  output W,
  output [4:0] DA,
  output R,
  output [4:0] A,
  output [4:0] B
);

  wire add, \and , and_1_out, and_4_out, and_9_out, and_12_out, and_13_out, and_14_out, and_18_out,
       and_19_out, beq, bgtz, blez, bltz, bne, comparator_1_lt, comparator_2_gt, comparator_2_lt,
       comparator_3_gt, comparator_5_eq, comparator_6_eq, comparator_7_eq, comparator_8_eq, comparator_15_eq,
       comparator_16_eq, comparator_17_eq, comparator_18_lt, comparator_19_eq, comparator_20_eq,
       comparator_21_lt, comparator_22_gt, comparator_22_lt, comparator_23_gt, comparator_24_eq,
       comparator_25_eq, comparator_26_eq, comparator_27_eq, comparator_29_eq, comparator_30_eq,
       comparator_31_eq, comparator_32_eq, comparator_33_eq, comparator_34_eq, comparator_35_eq,
       comparator_37_eq, comparator_38_eq, comparator_39_eq, comparator_40_eq, comparator_41_eq,
       comparator_42_eq, comparator_43_eq, comparator_44_eq, comparator_45_eq, comparator_46_eq,
       comparator_48_eq, comparator_49_eq, div, divu, halt, j, jr, kbd, lw, mfhi, mflo, mul, mulu, \nor ,
       OPCODE_0, \or , or_1_out, or_3_out, pop, push, rnd, stl, stlu, sub, sw, tty, \xor ;

  Comparator #(.width(6)) comparator_1 (.a(6'b001111), .b(in_1[31:26]), .lt(comparator_1_lt));  // open: gt, eq
  Comparator #(.width(6)) comparator_2 (
    .a(in_1[31:26]), .b(6'b001001), .gt(comparator_2_gt), .lt(comparator_2_lt));  // open: eq
  Comparator #(.width(6)) comparator_3 (.a(in_1[31:26]), .b(6'b000111), .gt(comparator_3_gt));  // open: eq, lt
  Comparator #(.width(6)) comparator_4 (.a(in_1[31:26]), .b({6{1'b0}}), .eq(OPCODE_0));  // open: gt, lt
  Comparator #(.width(11)) comparator_5 (.a(11'h20), .b(in_1[10:0]), .eq(comparator_5_eq));  // open: gt, lt
  Comparator #(.width(6)) comparator_6 (.a(6'b001000), .b(in_1[31:26]), .eq(comparator_6_eq));  // open: gt, lt
  Comparator #(.width(16)) comparator_7 (.a(16'h18), .b(in_1[15:0]), .eq(comparator_7_eq));  // open: gt, lt
  Comparator #(.width(16)) comparator_8 (.a(16'h1a), .b(in_1[15:0]), .eq(comparator_8_eq));  // open: gt, lt
  Comparator #(.width(6)) comparator_9 (.a(6'b000010), .b(in_1[31:26]), .eq(j));  // open: gt, lt
  Comparator #(.width(21)) comparator_10 (.a(21'h8), .b(in_1[20:0]), .eq(jr));  // open: gt, lt
  Comparator #(.width(6)) comparator_11 (.a(6'b000100), .b(in_1[31:26]), .eq(beq));  // open: gt, lt
  Comparator #(.width(6)) comparator_12 (.a(6'b000101), .b(in_1[31:26]), .eq(bne));  // open: gt, lt
  or or_1 (or_1_out, comparator_2_gt, comparator_2_lt);
  and and_1 (and_1_out, OPCODE_0, comparator_5_eq);
  and and_2 (mul, OPCODE_0, comparator_7_eq);
  and and_3 (div, OPCODE_0, comparator_8_eq);
  and and_4 (and_4_out, comparator_1_lt, or_1_out, comparator_3_gt);
  or or_2 (add, and_1_out, comparator_6_eq);
  Multiplexer #(.width(5), .enable("false")) multiplexer_1 (
    .in0(in_1[20:16]), .in1(in_1[15:11]), .out(DA), .sel(and_4_out));
  Comparator #(.width(6)) comparator_13 (.a(6'b000110), .b(in_1[31:26]), .eq(blez));  // open: gt, lt
  Comparator #(.width(6)) comparator_14 (.a(6'b000111), .b(in_1[31:26]), .eq(bgtz));  // open: gt, lt
  Comparator #(.width(11)) comparator_15 (.a(11'h22), .b(in_1[10:0]), .eq(comparator_15_eq));  // open: gt, lt
  Comparator #(.width(16)) comparator_16 (.a(16'h19), .b(in_1[15:0]), .eq(comparator_16_eq));  // open: gt, lt
  Comparator #(.width(16)) comparator_17 (.a(16'h1b), .b(in_1[15:0]), .eq(comparator_17_eq));  // open: gt, lt
  Comparator #(.width(32)) comparator_18 (.a(in_1), .b(32'hfc00003f), .eq(halt), .lt(comparator_18_lt));  // open: gt
  Comparator #(.width(6)) comparator_19 (.a({6{1'b1}}), .b(in_1[31:26]), .eq(comparator_19_eq));  // open: gt, lt
  and and_5 (tty, comparator_19_eq, comparator_20_eq);
  Comparator #(.width(21)) comparator_20 (.a(21'h1), .b(in_1[20:0]), .eq(comparator_20_eq));  // open: gt, lt
  and and_6 (sub, OPCODE_0, comparator_15_eq);
  and and_7 (mulu, OPCODE_0, comparator_16_eq);
  and and_8 (divu, OPCODE_0, comparator_17_eq);
  Comparator #(.width(6)) comparator_21 (.a(6'b001000), .b(in_1[31:26]), .lt(comparator_21_lt));  // open: gt, eq
  Comparator #(.width(6)) comparator_22 (
    .a(in_1[31:26]), .b(6'b000011), .gt(comparator_22_gt), .lt(comparator_22_lt));  // open: eq
  Comparator #(.width(6)) comparator_23 (.a(in_1[31:26]), .b({6{1'b0}}), .gt(comparator_23_gt));  // open: eq, lt
  Comparator #(.width(16)) comparator_24 (.a(16'hfc00), .b(in_1[31:16]), .eq(comparator_24_eq));  // open: gt, lt
  Comparator #(.width(11)) comparator_25 (.a(11'h2), .b(in_1[10:0]), .eq(comparator_25_eq));  // open: gt, lt
  Comparator #(.width(16)) comparator_26 (.a(16'hfc00), .b(in_1[31:16]), .eq(comparator_26_eq));  // open: gt, lt
  Comparator #(.width(11)) comparator_27 (.a(11'h3), .b(in_1[10:0]), .eq(comparator_27_eq));  // open: gt, lt
  Comparator #(.width(6)) comparator_28 (.a(6'b000001), .b(in_1[31:26]), .eq(bltz));  // open: gt, lt
  and and_9 (and_9_out, comparator_21_lt, or_3_out, comparator_23_gt);
  or or_3 (or_3_out, comparator_22_gt, comparator_22_lt);
  Comparator #(.width(11)) comparator_29 (.a(11'h2a), .b(in_1[10:0]), .eq(comparator_29_eq));  // open: gt, lt
  Comparator #(.width(6)) comparator_30 (.a(6'b001010), .b(in_1[31:26]), .eq(comparator_30_eq));  // open: gt, lt
  Comparator #(.width(11)) comparator_31 (.a(11'h24), .b(in_1[10:0]), .eq(comparator_31_eq));  // open: gt, lt
  Comparator #(.width(6)) comparator_32 (.a(6'b001100), .b(in_1[31:26]), .eq(comparator_32_eq));  // open: gt, lt
  Comparator #(.width(11)) comparator_33 (.a(11'h25), .b(in_1[10:0]), .eq(comparator_33_eq));  // open: gt, lt
  Comparator #(.width(6)) comparator_34 (.a(6'b001101), .b(in_1[31:26]), .eq(comparator_34_eq));  // open: gt, lt
  and and_10 (rnd, comparator_24_eq, comparator_25_eq);
  and and_11 (kbd, comparator_26_eq, comparator_27_eq);
  or or_4 (jump, and_9_out, comparator_35_eq);
  and and_12 (and_12_out, OPCODE_0, comparator_29_eq);
  and and_13 (and_13_out, OPCODE_0, comparator_31_eq);
  and and_14 (and_14_out, OPCODE_0, comparator_33_eq);
  Comparator #(.width(27)) comparator_35 (
    .a({in_1[31:26], in_1[20:0]}), .b(27'h8), .eq(comparator_35_eq));  // open: gt, lt
  or or_5 (stl, and_12_out, comparator_30_eq);
  or or_6 (\and , and_13_out, comparator_32_eq);
  or or_7 (\or , and_14_out, comparator_34_eq);
  Comparator #(.width(6)) comparator_36 (.a(6'b100011), .b(in_1[31:26]), .eq(lw));  // open: gt, lt
  Comparator #(.width(16)) comparator_37 (.a(16'he000), .b(in_1[31:16]), .eq(comparator_37_eq));  // open: gt, lt
  and and_15 (pop, comparator_37_eq, comparator_38_eq);
  Comparator #(.width(11)) comparator_38 (.a({11{1'b0}}), .b(in_1[10:0]), .eq(comparator_38_eq));  // open: gt, lt
  Comparator #(.width(11)) comparator_39 (.a(11'h12), .b(in_1[10:0]), .eq(comparator_39_eq));  // open: gt, lt
  Comparator #(.width(16)) comparator_40 (.a({16{1'b0}}), .b(in_1[31:16]), .eq(comparator_40_eq));  // open: gt, lt
  Comparator #(.width(11)) comparator_41 (.a(11'h12), .b(in_1[10:0]), .eq(comparator_41_eq));  // open: gt, lt
  Priority_Encoder #(.select(5)) priority_encoder_1 (
    .in1(add), .in2(sub), .in3(mul), .in4(mulu), .in5(div), .in6(divu), .in7(stl), .in8(stlu), .in9(\and ),
    .in10(\or ), .in11(\nor ), .in12(\xor ), .in13(beq), .in14(bne), .in15(blez), .in16(bgtz), .in17(bltz),
    .in18(j), .in19(jr), .in20(mflo), .in21(mfhi), .in22(lw), .in23(sw), .in24(pop), .in25(push),
    .in26(halt), .in27(tty), .in28(rnd), .in29(kbd), .out(Op));  // open: in0, in30, in31, gs, en_out, en_in
  Comparator #(.width(11)) comparator_42 (.a(11'h2b), .b(in_1[10:0]), .eq(comparator_42_eq));  // open: gt, lt
  Comparator #(.width(6)) comparator_43 (.a(6'b001011), .b(in_1[31:26]), .eq(comparator_43_eq));  // open: gt, lt
  Comparator #(.width(11)) comparator_44 (.a(11'h28), .b(in_1[10:0]), .eq(comparator_44_eq));  // open: gt, lt
  Comparator #(.width(6)) comparator_45 (.a(6'b001110), .b(in_1[31:26]), .eq(comparator_45_eq));  // open: gt, lt
  Comparator #(.width(11)) comparator_46 (.a(11'h27), .b(in_1[10:0]), .eq(comparator_46_eq));  // open: gt, lt
  and and_16 (mflo, comparator_39_eq, comparator_40_eq);
  and and_17 (mfhi, comparator_40_eq, comparator_41_eq);
  and and_18 (and_18_out, OPCODE_0, comparator_42_eq);
  and and_19 (and_19_out, OPCODE_0, comparator_44_eq);
  and and_20 (\nor , OPCODE_0, comparator_46_eq);
  nor nor_1 (Save_in_registers, beq, bne, blez, bgtz, bltz, j, jr, sw, push, halt, tty);
  or or_8 (W, sw, push);
  or or_9 (R, lw, pop);
  or or_10 (stlu, and_18_out, comparator_43_eq);
  or or_11 (\xor , and_19_out, comparator_45_eq);
  Comparator #(.width(6)) comparator_47 (.a(6'b101011), .b(in_1[31:26]), .eq(sw));  // open: gt, lt
  Comparator #(.width(6)) comparator_48 (.a(6'b111000), .b(in_1[31:26]), .eq(comparator_48_eq));  // open: gt, lt
  and and_21 (push, comparator_48_eq, comparator_49_eq);
  Comparator #(.width(21)) comparator_49 (.a(21'h1), .b(in_1[20:0]), .eq(comparator_49_eq));  // open: gt, lt

  assign A = in_1[20:16];
  assign B = in_1[25:21];

  // Other names for the same wires on the sheet: Big_part_of_it[20:0] = in_1[20:0]; End[10:0] = in_1[10:0];
  //   Func_Code[5:0] = in_1[5:0]; IConstant[15:0] = in_1[15:0]; Instruction[31:0] = in_1; J_Value[25:0] = in_1[25:0];
  //   x[4:0] = in_1[10:6]; RD[4:0] = in_1[15:11]; I_Constant[15:0] = K; RT[4:0] = in_1[20:16];
  //   Start[15:0] = in_1[31:16]; RS[4:0] = in_1[25:21]; Op_Code[5:0] = in_1[31:26]

  // Notes on the sheet:
  //   ADD
  //   MUL
  //   DIV
  //   OPERACIONES JUMP
  //   SEPARANDO LA ENTRADA
  //   OPERACIONES ARITMETICAS
  //   JUMP
  //   JUMP
  //   REG
  //   BEQ
  //   BNE
  //   OBTENIENDO DIRECCION
  //   EN LA CUAL SE ESCRIBE
  //   SUB
  //   Halt
  //   OPERACIONES ESPECIALES
  //   MULU
  //   DIVU
  //   TTY
  //   BLEZ
  //   BGTZ
  //   INSTRUCTION
  //   DECODER
  //   OPERACIONES BRANCH
  //   INSTRUCCION DE SALTO
  //   OPERADORES
  //   SET RANDOM
  //   SET KEY
  //   BLTZ
  //   CONSTANTE
  //   PARA INMEDIATES
  //   STL
  //   AND
  //   OR
  //   DA LA OPERACION
  //   LOAD W
  //   POP FROM STACK
  //   OPERACIONES MOVE
  //   STLU
  //   XOR
  //   NOR
  //   READ/WRITE
  //   MOVE FROM LO
  //   MOVE FROM HI
  //   SE ESCRIBIRA EN LA RAM
  //   SE LEERA DE LA RAM
  //   STORE W
  //   PUSH IN STAK
  //   GUARDA EN
  //   LOS REGISTROS
endmodule
